# Fritzing sketch led+pot+button (saved by Fritzing 0.9.3b)
breadboards: 1

parts:
  LED2 = LED - 5mm [color="Orange (612nm)" package="5 mm [THT]"]
  LED3 = LED - 5mm [color="Green (570nm)" package="5 mm [THT]"]
  Composant1 = Arduino Uno (Rev3)
  U1 = POT [package=pot_mammoth]
  S1 = Momentary Switch [package=ksa_sealed_tac_switch]
  R1 = Resistor [tolerance=±5% resistance=220 package=THT]
  LED1 = LED - 5mm [color="Red (633nm)" package="5 mm [THT]"]

nets:
  N1: LED2.cathode, LED3.cathode, Composant1.GND, U1.E, R1.Pin_1, LED1.cathode
  N2: LED2.anode, Composant1.D5_PWM
  N3: LED3.anode, Composant1.D6_PWM
  N4: Composant1.A0, U1.A
  N5: Composant1.D11_PWM/MOSI, S1.2
  N6: Composant1.D3_PWM, LED1.anode
  N7: Composant1.5V, U1.S, S1.3
  N8: S1.1, R1.Pin_0
